# Fritzing sketch treenhouse sketch (saved by Fritzing 0.9.3b)
perfboards: 1

parts:
  Bauteil1 = Arduino Uno (Rev3) - ICSP
  RHT1 = Humidity and Temperature Sensor RHT03
  Bauteil2 = Barometric Pressure Sensor - BMP085 Breakout
  HC-SR04_Sensor_1 = HC-SR04 Ultrasonic Distance Sensor
  U1 = ESP8266 WiFi Module [part_number=ESP8266]
  J3 = double row male pin header, 8 pins [form="♂ (male)"]
  J4 = double row male pin header, 10 pins [form="♂ (male)"]
  J5 = double row male pin header, 8 pins [form="♂ (male)"]
  DS1 = DS18B20 1-Wire Temperature Sensor [part_number=DS18B20]
  J2 = double row female pin header, 10 pins [form="♀ (female)"]
  J6 = double row male pin header, 6 pins [form="♂ (male)"]
  R1 = Resistor [tolerance=±5% resistance=4.7k package=THT]  # not connected
  IC1 = DS1307 [package=THT]

nets:
  N1: Bauteil1.A4/SDA, Bauteil2.SDA, J2.pin4, J6.pin5, IC1.SDA_-_I2C_Data
  N2: Bauteil1.A5/SCL, Bauteil2.SCL, J2.pin5, J6.pin6, IC1.SCL_-_I2C_Clock
  5V: Bauteil1.5V, RHT1.Vcc, J3.pin4, DS1.VDD, J2.pin1, IC1.+V
  GND: Bauteil1.GND, RHT1.GND_2, Bauteil2.GND, HC-SR04_Sensor_1.ECHO, U1.GND, J4.pin4, DS1.GND, J2.pin3, IC1.0V
  N3: Bauteil1.D8, HC-SR04_Sensor_1.TRIG
  N4: Bauteil1.D0/RX, U1.RXD, J5.pin7
  N5: Bauteil1.D1/TX, U1.TXD, J5.pin8
  N6: Bauteil1.D2, J5.pin6, DS1.DQ, J2.pin7
  N7: Bauteil1.D4, HC-SR04_Sensor_1.GND
  N8: Bauteil1.D7, RHT1.Data-signal, J5.pin1, J2.pin6
  VCC: Bauteil1.3V3, Bauteil2.VCC, U1.VCC, U1.CH_PD, J3.pin3, J2.pin2
